# Fritzing sketch circuit_defi_evasion (saved by Fritzing 0.9.3b)
breadboards: 1

parts:
  Part1 = Arduino Nano (Rev3.0)
  R1 = Resistor [tolerance=±5% resistance=1k package=THT]
  R2 = Photocell (LDR) [part_number=BS-120E0F package=THT]
  LED1 = LED - 5mm [color="Red (633nm)" package="5 mm [THT]"]
  LED6 = LED - 5mm [color="Red (633nm)" package="5 mm [THT]"]
  LED7 = LED - 5mm [color="Green (560nm)" package="5 mm [THT]"]
  LED9 = LED - 5mm [color="Green (560nm)" package="5 mm [THT]"]

nets:
  N1: Part1.D2, LED7.anode
  N2: Part1.D3, LED9.anode
  N3: Part1.D4, LED1.anode
  N4: Part1.D5, LED6.anode
  N5: Part1.GND, LED1.cathode, LED6.cathode, LED7.cathode, LED9.cathode
  N6: Part1.5V, R1.Pin_0
  N7: Part1.A3, R2.pin_0
  N8: R1.Pin_1, R2.pin_1
